# Fritzing sketch Jura-ArduinoUno (saved by Fritzing 0.9.3b)
circuit board: 10cm x 6cm

parts:
  Arduino_Uno = Arduino Uno (Rev3) - ICSP
  Coffeemaker = male pin header, 5 pins [form="♂ (male)"]

nets:
  N1: Arduino_Uno.GND, Coffeemaker.pin4
  N2: Arduino_Uno.D2, Coffeemaker.pin5
  N3: Arduino_Uno.D3_PWM, Coffeemaker.pin3
  5V: Coffeemaker.pin1
